# Fritzing sketch CircuitV1 (saved by Fritzing 0.9.3b)
stripboards: 1

parts:
  M1 = DOIT Esp32 DevKit v1 (30 pins long, 11 pins width) [part_number=ESP32S-PIN30]
  MD09B1 = A4988 Stepper Motor Driver Carrier
  MD09B2 = A4988 Stepper Motor Driver Carrier
  M2 = Stepper Motor - Bipolar
  M3 = Stepper Motor - Bipolar
  BAT1 = BC9VPC [package=bc9vpc]

nets:
  VDD: M1.3V3, MD09B1.VDD, MD09B2.VDD
  N1: M1.GND, MD09B1.GROUND#147, MD09B2.GROUND#147
  N2: M1.D35, MD09B1.MS3
  N3: M1.D32, MD09B2.MS3
  N4: M1.D27, MD09B1.STEP
  N5: M1.D14, MD09B1.DIR
  N6: M1.D12, MD09B2.STEP
  N7: M1.D13, MD09B2.DIR
  N8: MD09B1.RESET, MD09B1.SLEEP
  N9: MD09B1.VMOT, MD09B2.VMOT, BAT1.V+
  N10: MD09B1.GROUND#141, MD09B2.GROUND#141, BAT1.V-
  N11: MD09B1.OUT_2B, M2.A
  N12: MD09B1.OUT_2A, M2.C
  N13: MD09B1.OUT_1A, M2.B
  N14: MD09B1.OUT_1B, M2.D
  N15: MD09B2.RESET, MD09B2.SLEEP
  N16: MD09B2.OUT_2B, M3.A
  N17: MD09B2.OUT_2A, M3.C
  N18: MD09B2.OUT_1A, M3.B
  N19: MD09B2.OUT_1B, M3.D

custom parts:
  DOIT Esp32 DevKit v1 (30 pins long, 11 pins width): The DOIT Esp32 DevKit v1 is one of the development board created by DOIT to evaluate the ESP-WROOM-32 module. It is based on the ESP32 microcontroller that boasts Wifi, Bluetooth, Ethernet and Low Power support all in a single chip. (vanepp) made breadboard work, adjusted pin numbering and labels and reduced size of schematic and cleaned up pcb. This chip is 30pins long (2 x15) and 11 pins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
