# Fritzing sketch CircuitV2 (saved by Fritzing 0.9.3b)
stripboards: 1

parts:
  M1 = DOIT Esp32 DevKit v1 (30 pins long, 11 pins width) [part_number=ESP32S-PIN30]
  MD09B1 = A4988 Stepper Motor Driver Carrier
  MD09B2 = A4988 Stepper Motor Driver Carrier
  M2 = Stepper Motor - Bipolar
  M3 = Stepper Motor - Bipolar
  BAT1 = BC9VPC [package=bc9vpc]
  F1 = FUSE [package=fuse_5mm]
  C1 = Capacitor Polarized [package=panasonic_c]

nets:
  VDD: M1.3V3, MD09B1.VDD, MD09B2.VDD
  N1: M1.GND, MD09B1.GROUND#147, MD09B2.GROUND
  N2: M1.D2, MD09B1.DIR
  N3: M1.D4, MD09B1.STEP
  N4: M1.RX2, MD09B1.MS3
  N5: M1.TX2, MD09B1.MS2
  N6: M1.D5, MD09B1.MS1
  N7: M1.D26, MD09B2.MS1
  N8: M1.D27, MD09B2.MS2
  N9: M1.D14, MD09B2.MS3
  N10: M1.D12, MD09B2.STEP
  N11: M1.D13, MD09B2.DIR
  N12: MD09B1.RESET, MD09B1.SLEEP
  N13: MD09B1.VMOT, BAT1.V+, C1.+
  N14: MD09B1.GROUND#141, BAT1.V-, F1.1, F1.2, C1.-
  N15: MD09B1.OUT_2B, M2.A
  N16: MD09B1.OUT_2A, M2.C
  N17: MD09B1.OUT_1A, M2.B
  N18: MD09B1.OUT_1B, M2.D
  N19: MD09B2.RESET, MD09B2.SLEEP
  N20: MD09B2.OUT_2B, M3.A
  N21: MD09B2.OUT_2A, M3.C
  N22: MD09B2.OUT_1A, M3.B
  N23: MD09B2.OUT_1B, M3.D

custom parts:
  DOIT Esp32 DevKit v1 (30 pins long, 11 pins width): The DOIT Esp32 DevKit v1 is one of the development board created by DOIT to evaluate the ESP-WROOM-32 module. It is based on the ESP32 microcontroller that boasts Wifi, Bluetooth, Ethernet and Low Power support all in a single chip. (vanepp) made breadboard work, adjusted pin numbering and labels and reduced size of schematic and cleaned up pcb. This chip is 30pins long (2 x15) and 11 pins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
