# Fritzing sketch CircuitV3 (saved by Fritzing 0.9.3b)
stripboards: 1

parts:
  M1 = DOIT Esp32 DevKit v1 (30 pins long, 11 pins width) [part_number=ESP32S-PIN30]
  MD09B1 = A4988 Stepper Motor Driver Carrier
  MD09B2 = A4988 Stepper Motor Driver Carrier
  M2 = Stepper Motor - Bipolar
  M3 = Stepper Motor - Bipolar
  BAT1 = BC9VPC [package=bc9vpc]
  F1 = FUSE [package=fuse_5mm]
  C1 = Capacitor Polarized [package=panasonic_c]
  C2 = Capacitor Polarized [package=panasonic_c]

nets:
  VDD: M1.3V3, MD09B1.VDD, MD09B2.VDD
  GND: M1.GND, M1.VIN, MD09B1.VMOT, MD09B1.GROUND, MD09B2.VMOT, MD09B2.GROUND, BAT1.V+, BAT1.V-, F1.1, F1.2, C1.+, C1.-, C2.+, C2.-
  N1: M1.D21, MD09B2.MS1
  N2: M1.RX0, MD09B2.MS2
  N3: M1.TX0, MD09B2.MS3
  N4: M1.D22, MD09B2.STEP
  N5: M1.D23, MD09B2.DIR
  N6: M1.D32, MD09B1.DIR
  N7: M1.D33, MD09B1.STEP
  N8: M1.D25, MD09B1.MS3
  N9: M1.D26, MD09B1.MS2
  N10: M1.D27, MD09B1.MS1
  N11: MD09B1.RESET, MD09B1.SLEEP
  N12: MD09B1.OUT_2B, M2.A
  N13: MD09B1.OUT_2A, M2.C
  N14: MD09B1.OUT_1A, M2.B
  N15: MD09B1.OUT_1B, M2.D
  N16: MD09B2.RESET, MD09B2.SLEEP
  N17: MD09B2.OUT_2B, M3.A
  N18: MD09B2.OUT_2A, M3.C
  N19: MD09B2.OUT_1A, M3.B
  N20: MD09B2.OUT_1B, M3.D

custom parts:
  DOIT Esp32 DevKit v1 (30 pins long, 11 pins width): The DOIT Esp32 DevKit v1 is one of the development board created by DOIT to evaluate the ESP-WROOM-32 module. It is based on the ESP32 microcontroller that boasts Wifi, Bluetooth, Ethernet and Low Power support all in a single chip. (vanepp) made breadboard work, adjusted pin numbering and labels and reduced size of schematic and cleaned up pcb. This chip is 30pins long (2 x15) and 11 pins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
